// Logisim project Practica02.circ as structural Verilog: 4 circuits, main circuit main
module main (
  input  A,
  input  B,
  input  A_2,
  input  B_2,
  input  A_3,
  input  B_3,
  input  A_4,
  output out_8,
  output out_9,
  output out_10,
  output out_11
);

  wire pull_resistor_2_node, transistor_1_out, transistor_6_out, transistor_7_out, transistor_10_out;

  Transistor #(.\type ("n")) transistor_1 (.in(1'b1), .out(transistor_1_out), .gate(A));
  Transistor #(.\type ("n")) transistor_2 (.in(1'b1), .out(out_10), .gate(A_3));
  Transistor #(.\type ("n")) transistor_3 (.in(transistor_1_out), .out(out_8), .gate(B));
  Transistor #(.\type ("n")) transistor_4 (.in(1'b1), .out(out_10), .gate(B_3));
  Transistor transistor_5 (.in(1'b1), .out(out_11), .gate(A_4));
  Transistor transistor_6 (.in(transistor_7_out), .out(transistor_6_out), .gate(A_2));
  Transistor #(.\type ("n")) transistor_7 (.in(1'b1), .out(transistor_7_out), .gate(B_2));
  Pull_Resistor pull_resistor_1 (.node(transistor_6_out));
  Transistor #(.\type ("n")) transistor_8 (.in(1'b1), .out(out_9), .gate(transistor_6_out));
  Transistor #(.\type ("n"), .gate("br")) transistor_9 (.in(1'b1), .out(out_9), .gate(pull_resistor_2_node));
  Transistor #(.\type ("n")) transistor_10 (.in(1'b1), .out(transistor_10_out), .gate(A_2));
  Pull_Resistor pull_resistor_2 (.node(pull_resistor_2_node));
  Transistor transistor_11 (.in(transistor_10_out), .out(pull_resistor_2_node), .gate(B_2));

  // Notes on the sheet:
  //   AND
  //   OR
endmodule

module Ejercicio_2 (
  input  in_1,
  input  in_2,
  input  in_3,
  output out_4
);

  wire and_1_out, and_2_out, not_1_out, not_2_out;

  and and_1 (and_1_out, in_1, not_1_out, in_3);
  not not_1 (not_1_out, in_2);
  or or_1 (out_4, and_1_out, and_2_out);
  not not_2 (not_2_out, in_3);
  and and_2 (and_2_out, in_1, in_2, not_2_out);

  // Notes on the sheet:
  //   Llaves
  //   Switch
  //   Sensor
endmodule

module Ejercicio_3 (
  input  in_1,
  input  in_2,
  input  in_3,
  input  in_4,
  input  in_5,
  input  in_6,
  input  in_7,
  input  in_8,
  input  in_9,
  input  in_10,
  input  in_11,
  input  in_12,
  output out_13,
  output out_14,
  output out_15
);

  wire and_1_out, and_2_out, and_3_out, and_4_out, and_5_out, and_6_out, and_7_out, and_8_out, and_9_out,
       and_10_out, not_1_out, not_2_out, not_3_out, not_4_out, not_5_out, not_6_out, not_7_out, not_8_out;

  not not_1 (not_1_out, in_1);
  not not_2 (not_2_out, in_2);
  and and_1 (and_1_out, not_1_out, in_3);
  and and_2 (and_2_out, not_1_out, not_2_out, in_4);
  or or_1 (out_13, and_1_out, and_2_out, and_3_out);
  and and_3 (and_3_out, not_2_out, in_3, in_4);
  not not_3 (not_3_out, in_9);
  and and_4 (and_4_out, not_3_out, not_4_out, not_6_out, not_5_out);
  not not_4 (not_4_out, in_10);
  and and_5 (and_5_out, in_9, not_4_out, in_11, not_5_out);
  or or_2 (out_15, and_4_out, and_5_out, and_6_out, and_8_out);
  and and_6 (and_6_out, not_3_out, in_10, not_6_out, in_12);
  and and_7 (and_7_out, in_5, not_7_out);
  not not_5 (not_5_out, in_12);
  not not_6 (not_6_out, in_11);
  and and_8 (and_8_out, in_9, in_10, in_11, in_12);
  and and_9 (and_9_out, in_6, not_7_out, not_8_out);
  or or_3 (out_14, and_7_out, and_9_out, and_10_out);
  not not_7 (not_7_out, in_7);
  and and_10 (and_10_out, in_5, in_6, not_8_out);
  not not_8 (not_8_out, in_8);

  // Notes on the sheet:
  //   X
  //   X<Y
  //   Y
  //   X
  //   X=Y
  //   X
  //   Y
  //   X>Y
  //   Y
endmodule

module Ejercicio_4 (
  input  in_1,
  input  B,
  input  C,
  input  D,
  output out_5
);

  wire and_1_out, and_2_out, not_1_out, not_2_out, or_1_out, or_3_out;

  and and_1 (and_1_out, in_1, or_1_out);
  or or_1 (or_1_out, B, not_1_out, not_2_out);
  or or_2 (out_5, and_1_out, and_2_out);
  not not_1 (not_1_out, C);
  or or_3 (or_3_out, B, not_2_out);
  and and_2 (and_2_out, or_3_out, not_1_out);
  not not_2 (not_2_out, D);

  // Notes on the sheet:
  //   A
endmodule
