// Logisim project Practica 4.circ as structural Verilog
module Automata (
  input  Input,
  input  in_2
);

  wire and_1_out, and_2_out, and_3_out, clock_1_out, not_1_out, s_r_ff_1_qn, s_r_ff_2_qn;
  wire [1:0] s_r_ff_2_q;

  not not_1 (not_1_out, Input);
  and and_1 (and_1_out, s_r_ff_1_qn, not_1_out, s_r_ff_2_q[0]);
  and and_2 (and_2_out, s_r_ff_2_q[1], not_1_out, s_r_ff_2_q[0]);
  and and_3 (and_3_out, not_1_out, s_r_ff_2_qn);
  Clock clock_1 (.out(clock_1_out));
  S_R_Flip_Flop s_r_ff_1 (
    .S(and_1_out), .clk(clock_1_out), .R(and_2_out), .Q(s_r_ff_2_q[1]), .Qn(s_r_ff_1_qn));  // open: preset, reset, en
  S_R_Flip_Flop s_r_ff_2 (
    .S(and_3_out), .clk(clock_1_out), .R(s_r_ff_2_q[0]), .Q(s_r_ff_2_q[0]), .Qn(s_r_ff_2_qn));  // open: preset, reset, en
  Hex_Digit_Display hex_digit_display_1 (.value({{2{in_2}}, s_r_ff_2_q}));  // open: dp

  // Notes on the sheet:
  //   Circuito: Automata.
endmodule

module Registro_8_bits (
  input  [7:0] in_1,
  output [7:0] out_2
);

  wire clock_1_out;

  Clock clock_1 (.out(clock_1_out));
  D_Flip_Flop d_ff_1 (.clk(clock_1_out), .D(in_1[0]), .Q(out_2[0]));  // open: Qn, preset, en, reset
  D_Flip_Flop d_ff_2 (.clk(clock_1_out), .D(in_1[1]), .Q(out_2[1]));  // open: Qn, preset, en, reset
  D_Flip_Flop d_ff_3 (.clk(clock_1_out), .D(in_1[2]), .Q(out_2[2]));  // open: Qn, preset, en, reset
  D_Flip_Flop d_ff_4 (.clk(clock_1_out), .D(in_1[3]), .Q(out_2[3]));  // open: Qn, preset, en, reset
  D_Flip_Flop d_ff_5 (.clk(clock_1_out), .D(in_1[4]), .Q(out_2[4]));  // open: Qn, preset, en, reset
  D_Flip_Flop d_ff_6 (.clk(clock_1_out), .D(in_1[5]), .Q(out_2[5]));  // open: Qn, preset, en, reset
  D_Flip_Flop d_ff_7 (.clk(clock_1_out), .D(in_1[6]), .Q(out_2[6]));  // open: Qn, preset, en, reset
  D_Flip_Flop d_ff_8 (.clk(clock_1_out), .D(in_1[7]), .Q(out_2[7]));  // open: Qn, preset, en, reset
endmodule

module Shift_Register (
  input  in_1,
  output out_2,
  output out_3,
  output out_4,
  output out_5,
  output out_6,
  output out_7,
  output out_8,
  output out_9,
  output out_10
);

  wire clock_1_out;

  Clock clock_1 (.out(clock_1_out));
  D_Flip_Flop d_ff_1 (.clk(clock_1_out), .D(in_1), .Q(out_2));  // open: Qn, preset, en, reset
  D_Flip_Flop d_ff_2 (.clk(clock_1_out), .D(out_2), .Q(out_3));  // open: Qn, preset, en, reset
  D_Flip_Flop d_ff_3 (.clk(clock_1_out), .D(out_3), .Q(out_4));  // open: Qn, preset, en, reset
  D_Flip_Flop d_ff_4 (.clk(clock_1_out), .D(out_4), .Q(out_5));  // open: Qn, preset, en, reset
  D_Flip_Flop d_ff_5 (.clk(clock_1_out), .D(out_5), .Q(out_6));  // open: Qn, preset, en, reset
  D_Flip_Flop d_ff_6 (.clk(clock_1_out), .D(out_7), .Q(out_8));  // open: Qn, preset, en, reset
  D_Flip_Flop d_ff_7 (.clk(clock_1_out), .D(out_6), .Q(out_7));  // open: Qn, preset, en, reset
  D_Flip_Flop d_ff_8 (.clk(clock_1_out), .D(out_8), .Q(out_9));  // open: Qn, preset, en, reset

  assign out_10 = out_9;

  // Notes on the sheet:
  //   Circuito: Shift Register.
endmodule

module Banco_de_Registro (
  input  in_1,
  input  [7:0] in_2,
  input  [1:0] in_3,
  input  [1:0] in_4,
  input  [1:0] in_5,
  input  Escribir,
  input  [1:0] in_7,
  input  [7:0] in_8,
  output [7:0] out_9,
  output [7:0] out_10
);

  wire demultiplexer_2_out0, demultiplexer_2_out1, demultiplexer_2_out2, demultiplexer_2_out3,
       demultiplexer_4_out0, demultiplexer_4_out1, demultiplexer_4_out2, demultiplexer_4_out3;
  wire [7:0] demultiplexer_1_out0, demultiplexer_1_out1, demultiplexer_1_out2, demultiplexer_1_out3,
       demultiplexer_3_out0, demultiplexer_3_out1, demultiplexer_3_out2, demultiplexer_3_out3,
       registro_de_8_bits_auxiliar_3_out_3, registro_de_8_bits_auxiliar_4_out_3,
       registro_de_8_bits_auxiliar_5_out_3, registro_de_8_bits_auxiliar_6_out_3;

  Demultiplexer #(.select(2), .width(8), .enable("false")) demultiplexer_1 (
    .out0(demultiplexer_1_out0), .out1(demultiplexer_1_out1), .out2(demultiplexer_1_out2),
    .out3(demultiplexer_1_out3), .in(in_8), .sel(in_7));
  Demultiplexer #(.select(2), .enable("false")) demultiplexer_2 (
    .out0(demultiplexer_2_out0), .out1(demultiplexer_2_out1), .out2(demultiplexer_2_out2),
    .out3(demultiplexer_2_out3), .in(in_1), .sel(in_3));
  Demultiplexer #(.select(2), .width(8), .enable("false")) demultiplexer_3 (
    .out0(demultiplexer_3_out0), .out1(demultiplexer_3_out1), .out2(demultiplexer_3_out2),
    .out3(demultiplexer_3_out3), .in(in_2), .sel(in_3));
  Demultiplexer #(.select(2), .enable("false")) demultiplexer_4 (
    .out0(demultiplexer_4_out0), .out1(demultiplexer_4_out1), .out2(demultiplexer_4_out2),
    .out3(demultiplexer_4_out3), .in(Escribir), .sel(in_7));
  Registro_de_8_bits_auxiliar registro_de_8_bits_auxiliar_1 (
    .in_2(demultiplexer_1_out0), .in_1(demultiplexer_4_out0));  // open: out_3
  Registro_de_8_bits_auxiliar registro_de_8_bits_auxiliar_2 (
    .in_2(demultiplexer_1_out1), .in_1(demultiplexer_4_out1));  // open: out_3
  Registro_de_8_bits_auxiliar registro_de_8_bits_auxiliar_3 (
    .in_2(demultiplexer_3_out0), .in_1(demultiplexer_2_out0), .out_3(registro_de_8_bits_auxiliar_3_out_3));
  Registro_de_8_bits_auxiliar registro_de_8_bits_auxiliar_4 (
    .in_2(demultiplexer_3_out1), .in_1(demultiplexer_2_out1), .out_3(registro_de_8_bits_auxiliar_4_out_3));
  Registro_de_8_bits_auxiliar registro_de_8_bits_auxiliar_5 (
    .in_2(demultiplexer_3_out2), .in_1(demultiplexer_2_out2), .out_3(registro_de_8_bits_auxiliar_5_out_3));
  Registro_de_8_bits_auxiliar registro_de_8_bits_auxiliar_6 (
    .in_2(demultiplexer_3_out3), .in_1(demultiplexer_2_out3), .out_3(registro_de_8_bits_auxiliar_6_out_3));
  Registro_de_8_bits_auxiliar registro_de_8_bits_auxiliar_7 (
    .in_2(demultiplexer_1_out2), .in_1(demultiplexer_4_out2));  // open: out_3
  Registro_de_8_bits_auxiliar registro_de_8_bits_auxiliar_8 (
    .in_2(demultiplexer_1_out3), .in_1(demultiplexer_4_out3));  // open: out_3
  Multiplexer #(.select(2), .width(8), .enable("false")) multiplexer_1 (
    .in0(registro_de_8_bits_auxiliar_3_out_3), .in1(registro_de_8_bits_auxiliar_4_out_3),
    .in2(registro_de_8_bits_auxiliar_5_out_3), .in3(registro_de_8_bits_auxiliar_6_out_3), .out(out_9),
    .sel(in_4));
  Multiplexer #(.select(2), .width(8), .enable("false")) multiplexer_2 (
    .in0(registro_de_8_bits_auxiliar_3_out_3), .in1(registro_de_8_bits_auxiliar_4_out_3),
    .in2(registro_de_8_bits_auxiliar_5_out_3), .in3(registro_de_8_bits_auxiliar_6_out_3), .out(out_10),
    .sel(in_5));

  // Notes on the sheet:
  //   Escribir registro
endmodule

module Registro_de_8_bits_auxiliar (
  input  in_1,
  input  [7:0] in_2,
  output [7:0] out_3
);

  D_Flip_Flop d_ff_1 (.clk(in_1), .D(in_2[0]), .Q(out_3[0]));  // open: Qn, preset, en, reset
  D_Flip_Flop d_ff_2 (.clk(in_1), .D(in_2[1]), .Q(out_3[1]));  // open: Qn, preset, en, reset
  D_Flip_Flop d_ff_3 (.clk(in_1), .D(in_2[2]), .Q(out_3[2]));  // open: Qn, preset, en, reset
  D_Flip_Flop d_ff_4 (.clk(in_1), .D(in_2[3]), .Q(out_3[3]));  // open: Qn, preset, en, reset
  D_Flip_Flop d_ff_5 (.clk(in_1), .D(in_2[4]), .Q(out_3[4]));  // open: Qn, preset, en, reset
  D_Flip_Flop d_ff_6 (.clk(in_1), .D(in_2[5]), .Q(out_3[5]));  // open: Qn, preset, en, reset
  D_Flip_Flop d_ff_7 (.clk(in_1), .D(in_2[6]), .Q(out_3[6]));  // open: Qn, preset, en, reset
  D_Flip_Flop d_ff_8 (.clk(in_1), .D(in_2[7]), .Q(out_3[7]));  // open: Qn, preset, en, reset
endmodule
